# Fritzing sketch arduino-brain-turn-in (saved by Fritzing 0.9.3b)
breadboards: 1

parts:
  Part1 = Arduino Uno (Rev3)
  LCD1 = LCD screen
  S1 = Pushbutton [package="[THT]"]
  S2 = Pushbutton [package="[THT]"]
  R1 = Resistor [tolerance=±5% resistance=10k package=THT]
  R2 = Resistor [tolerance=±5% resistance=10k package=THT]
  LED1 = RGB LED (com. cathode, rgb) [package="5 mm [THT]"]
  R3 = Resistor [tolerance=±5% resistance=220 package=THT]
  R5 = Resistor [tolerance=±5% resistance=220 package=THT]
  R6 = Resistor [tolerance=±5% resistance=220 package=THT]
  R7 = Rotary Potentiometer (Small) [maximum_resistance=100kΩ package=THT]
  R8 = Resistor [tolerance=±5% resistance=220 package=THT]

nets:
  N1: Part1.D8, LED1.blue_anode, R5.Pin_0
  N2: Part1.D9_PWM, LED1.green_anode, R6.Pin_0
  N3: Part1.D11_PWM/MOSI, LCD1.RS
  N4: Part1.D13/SCK, LED1.red_anode, R3.Pin_0
  N5: Part1.D2, LCD1.DB7
  N6: Part1.D3_PWM, LCD1.DB6
  N7: Part1.D4, LCD1.DB5
  N8: Part1.D5_PWM, LCD1.DB4
  N9: Part1.D6_PWM, S1.Pin_1, S1.Pin_2, R1.Pin_0
  N10: Part1.D7, S2.Pin_1, S2.Pin_2, R2.Pin_0
  5V: Part1.5V, LCD1.VDD, S1.Pin_3, S1.Pin_4, S2.Pin_3, S2.Pin_4, R3.Pin_1, R5.Pin_1, R6.Pin_1
  N11: LCD1.VSS, LCD1.LED-, R1.Pin_1, R2.Pin_1, LED1.common_cathode, R7.leg1, R7.leg2, R8.Pin_1
  N12: LCD1.V0, R7.wiper
  N13: LCD1.LED+, R8.Pin_0

notes:
  Sorry, no scematics here :(
